# Fritzing sketch LoadSide_Circuit (saved by Fritzing 0.8.7b)

parts:
  J1 = Power Jack [package=power_jack_combo]
  U1 = RELAY [package=relay-jzc]
  U2 = RELAY [package=relay-jzc]
  U3 = RELAY [package=relay-jzc]
  U4 = RELAY [package=relay-jzc]
  Part1 = ACS712 Low Current Sensor Board v12
  Part2 = ACS712 Low Current Sensor Board v12
  Part3 = ACS712 Low Current Sensor Board v12
  Part4 = ACS712 Low Current Sensor Board v12
  Part5 = LilyPad Tri-Color LED
  Part6 = LilyPad Tri-Color LED
  LED1 = LED - 5mm [color="Red (633nm)" package="5 mm [THT]"]
  LED2 = LED - 5mm [color="Red (633nm)" package="5 mm [THT]"]
  Part7 = Arduino Uno (Rev3)

nets:
  N1: J1.GND, LED2.anode
  N2: U1.COIL2, U2.COIL2
  N3: U1.NC, Part7.D5_PWM
  N4: U1.MAIN, Part1.IP-
  N5: U2.NC, Part7.D4
  N6: U2.MAIN, Part2.IP-
  N7: U3.COIL2, U4.COIL2, Part7.5V
  N8: U3.NC, Part7.D3_PWM
  N9: U3.MAIN, Part3.IP-
  N10: U4.NC, Part7.D2
  N11: U4.MAIN, Part4.IP-
  N12: Part1.IP+, Part5.+
  5V: Part1.5V, Part2.5V
  N13: Part1.VO, Part7.A0
  N14: Part2.IP+, Part6.+
  N15: Part2.VO, Part7.A1
  N16: Part3.IP+, LED1.cathode
  N17: Part3.VO, Part7.A2
  N18: Part4.IP+, LED2.cathode
  N19: Part4.VO, Part7.A3

notes:
  12V SMPS
  Relay 1
  Relay 2
  Relay 3
  Relay 4
  ACS712
  120W Load
  24W Load<module fritzingVersion="0.8.7b.01.24.1bf5">
  <boundingRects>
  <boundingRect rect="0 0 0 0" name="PCB View"/>
  <boundingRect rect="814.67 90.196 63.348 33" name="Breadboard View"/>
  <boundingRect rect="0 0 0 0" name="Schematic View"/>
  </boundingRects>
  <instances>
  <instance moduleIdRef="NoteModuleID" modelIndex="85413385" path=":/resources/parts/core/note.fzp">
  <title>Note3</title>
  <text>&lt;!DOCTYPE HTML PUBLIC "-//W3C//DTD HTML 4.0//EN" "http://www.w3.org/TR/REC-html40/strict.dtd">
  &lt;html>&lt;head>&lt;meta name="qrichtext" content="1" />&lt;style type="text/css">
  p, li { white-space: pre-wrap; }
  &lt;/style>&lt;/head>&lt;body style=" font-family:'Droid Sans'; font-size:9pt; font-weight:400; font-style:normal;">
  &lt;p style=" margin-top:0px; margin-bottom:0px; margin-left:0px; margin-right:0px; -qt-block-indent:0; text-indent:0px;">120W Load&lt;/p>&lt;/body>&lt;/html></text>
  <views>
  <breadboardView layer="breadboardNote">
  <geometry width="63.348" x="814.67" y="90.196" z="6.50002" height="33"/>
  </breadboardView>
  </views>
  </instance>
  </instances>
  </module>
  24W Load
  Arduino UNO
