# Fritzing sketch SourceSide_Circuit (saved by Fritzing 0.8.7b)

parts:
  Part1 = Arduino Uno (Rev3)
  U1 = G3VM-61E1 [package=g3vm-61e1]
  D1 = SOLAR-IXYS [package=solarbit-12x1]
  Part2 = ACS712 Low Current Sensor Board v12
  R1 = Resistor [tolerance=±5% resistance=220 package=THT]
  R2 = Resistor [tolerance=±5% resistance=220 package=THT]

nets:
  N1: Part1.A0, U1.P$4, D1.C, Part2.IP-, R2.Pin_1
  N2: Part1.A1, Part2.VO
  N3: Part1.D3_PWM, U1.P$5
  N4: Part1.5V, U1.P$6
  N5: Part1.GND, R1.Pin_1
  N6: U1.P$3, Part2.IP+

notes:
  Solar Panel
  Relay
  ACS712
  Arduino UNO
  Voltage Divider
